# Fritzing sketch Foam_Cutter (saved by Fritzing 1.0.3b)

parts:
  Mod1 = Raspberry Pi 4B
  VCC1 = Mean Well RD-65B Enclosed Switching AC-to-DC Power Supply, Dual Output, 5V-24V
  Part1 = TB6600 STEPPER MOTOR DRIVER
  Part3 = DEVMO XL4015 5A DC Buck Step-Down Adjustable Voltage Power Module Converter with LED Voltmeter
  Part2 = TB6600 STEPPER MOTOR DRIVER
  M3 = Stepper Motor - Bipolar
  M4 = Stepper Motor - Bipolar

nets:
  N1: Mod1.5V, VCC1.+V1, Part1.PUL+, Part1.DIR+, Part3.IN+, Part3.OUT+
  GND: Mod1.GND, VCC1.Gnd, VCC1.Com#3, Part3.IN-, Part3.OUT-
  N2: Mod1.GPIO4, Part1.ENA-
  N3: Mod1.GPIO17, Part1.DIR-
  N4: Mod1.GPIO22, Part1.PUL-
  N5: Mod1.GPIO23, Part2.PUL-
  N6: Mod1.GPIO24, Part2.DIR-
  N7: Mod1.GPIO25, Part2.ENA-
  VCC: VCC1.+V2, Part1.VCC, Part1.A+, Part1.ENA+, Part2.VCC, Part2.A+, Part2.PUL+, Part2.DIR+, Part2.ENA+, M3.A, M4.A
  GND_2: Part1.GND, Part2.GND
  N8: Part1.A-, M3.C
  N9: Part1.B+, M3.B
  N10: Part1.B-, M3.D
  N11: Part2.A-, M4.C
  N12: Part2.B+, M4.B
  N13: Part2.B-, M4.D

custom parts:
  Mean Well RD-65B Enclosed Switching AC-to-DC Power Supply, Dual Output, 5V-24V: Your standard 2x AA battery pack (3 Volts)
