# Fritzing sketch StepperDriverA4988 (saved by Fritzing 0.9.6b)

parts:
  Mod1 = Raspberry Pi 4B
  M1 = Stepper Motor - Bipolar
  Pololu_A1 = Pololu A4988 [package=SO16]

nets:
  3V3: Mod1.3V3, Pololu_A1.VDD
  N1: Mod1.GND, Mod1.GPIO15, Pololu_A1.GND#8
  N2: Mod1.GPIO27, Pololu_A1.MS1
  N3: Mod1.GPIO23, Pololu_A1.MS2
  N4: Mod1.GPIO24, Pololu_A1.MS3
  N5: Mod1.GPIO25, Pololu_A1.STEP
  N6: Mod1.GPIO5, Pololu_A1.DIR
  N7: M1.A, Pololu_A1.2B
  N8: M1.C, Pololu_A1.2A
  N9: M1.B, Pololu_A1.1A
  N10: M1.D, Pololu_A1.1B
  N11: Pololu_A1.RESET, Pololu_A1.SLEEP

notes:
  5.1 VDC, 3 Amps
  AC converter
  24 VDC, 5 Amps
  bench supply
  3.3 VDC provided by RaspPi
